# Fritzing sketch NapkinFire (saved by Fritzing 0.9.3b)
circuit board: 6.25cm x 6.25cm
breadboards: 1

parts:
  Adafruit_ESP32 = Adafruit HUZZAH32 ESP32 Feather [part_number="Adafruit #3405"]
  LOUD = Piezo Speaker [part_number=" COM-13940"]
  PIR = PIR sensor
  part = double row female pin header, 16 pins [form="♀ (female)"]
  part_2 = double row female pin header, 16 pins [form="♀ (female)"]
  part_3 = double row female pin header, 16 pins [form="♀ (female)"]
  part_4 = double row female pin header, 16 pins [form="♀ (female)"]
  Arducam = Arducam [package=THT]
  R1 = Resistor [tolerance=±5% resistance=220 package="0805 [SMD]"]
  beeper = Buzzer 12mm [package=buzzer-12mm]

nets:
  GND: Adafruit_ESP32.IO21, Adafruit_ESP32.IO17, Adafruit_ESP32.IO16, Adafruit_ESP32.GND, LOUD.pin1, PIR.GND, part.pin1, part.pin2, part.pin3, part.pin4, part.pin5, part.pin6, part.pin7, part.pin8, part.pin9, part.pin10, part.pin11, part.pin12, part.pin13, part.pin14, part.pin15, part.pin16, part_2.pin1, part_2.pin2, part_2.pin3, part_2.pin4, part_2.pin5, part_2.pin6, part_2.pin7, part_2.pin8, part_2.pin9, part_2.pin10, part_2.pin11, part_2.pin12, part_2.pin13, part_2.pin14, part_2.pin15, part_2.pin16, part_3.pin1, part_3.pin2, part_3.pin3, part_3.pin4, part_3.pin5, part_3.pin6, part_3.pin7, part_3.pin8, part_3.pin9, part_3.pin10, part_3.pin11, part_3.pin12, part_3.pin13, part_3.pin14, part_3.pin15, part_3.pin16, part_4.pin1, part_4.pin2, part_4.pin3, part_4.pin4, part_4.pin5, part_4.pin6, part_4.pin7, part_4.pin8, part_4.pin9, part_4.pin10, part_4.pin11, part_4.pin12, part_4.pin13, part_4.pin14, part_4.pin15, part_4.pin16, Arducam.GND, R1.Pin_1, beeper.1
  N1: Adafruit_ESP32.MISO, Arducam.MISO
  N2: Adafruit_ESP32.MOSI, Arducam.MOSI
  N3: Adafruit_ESP32.SCK, Arducam.SCK
  3.3V: Adafruit_ESP32.3.3V, PIR.VDD, Arducam.VCC, R1.Pin_0
  N4: Adafruit_ESP32.IO27_A10, PIR.SIG
  N5: Adafruit_ESP32.IO15_A8, beeper.2
  N6: Adafruit_ESP32.IO32_A7, LOUD.pin2
  N7: Adafruit_ESP32.IO14_A6, Arducam.CS
  N8: Adafruit_ESP32.SCL, Arducam.SCL
  N9: Adafruit_ESP32.SDA, Arducam.SDA

notes:
  3V
  0V
  IO1
  IO2
  IO3

custom parts:
  Arducam: A Arducam moudle
